// Logisim project BCD-to-7-Segment.circ as structural Verilog: 2 circuits, main circuit 74247
module _74247 (
  input  Input_A,
  input  Input_B,
  input  Input_C,
  input  Input_D,
  input  BI___RBO,
  input  LT,
  input  RBI,
  output Output_a,
  output Output_b,
  output Output_c,
  output Output_d,
  output Output_e,
  output Output_f,
  output Output_g
);

  wire and_1_out, and_2_out, and_3_out, and_4_out, and_5_out, and_6_out, and_7_out, and_8_out, and_9_out,
       and_10_out, and_11_out, and_12_out, and_13_out, and_14_out, and_15_out, and_16_out, and_17_out,
       buffer_1_out, buffer_2_out, buffer_3_out, nand_1_out, nand_2_out, nand_3_out, nand_5_out, nand_6_out,
       nand_7_out, nand_8_out, nor_1_out, nor_2_out, nor_3_out, nor_4_out, nor_5_out, nor_6_out, nor_7_out,
       not_1_out, not_2_out;

  nand nand_1 (nand_1_out, Input_A, buffer_1_out);
  nand nand_2 (nand_2_out, Input_B, buffer_1_out);
  nand nand_3 (nand_3_out, Input_C, buffer_1_out);
  not not_1 (not_1_out, Input_D);
  buf buffer_1 (buffer_1_out, LT);
  not not_2 (not_2_out, RBI);
  buf buffer_2 (buffer_2_out, BI___RBO);
  nand nand_4 (BI___RBO, buffer_1_out, not_2_out, not_1_out, nand_3_out, nand_2_out, nand_1_out);
  nand nand_5 (nand_5_out, nand_1_out, buffer_2_out);
  nand nand_6 (nand_6_out, nand_2_out, buffer_2_out);
  nand nand_7 (nand_7_out, nand_3_out, buffer_2_out);
  nand nand_8 (nand_8_out, not_1_out, buffer_2_out);
  and and_1 (and_1_out, nand_6_out, nand_8_out);
  and and_2 (and_2_out, nand_1_out, nand_2_out, nand_7_out);
  and and_3 (and_3_out, nand_5_out, nand_2_out, nand_3_out, not_1_out);
  and and_4 (and_4_out, nand_6_out, nand_8_out);
  and and_5 (and_5_out, nand_5_out, nand_2_out, nand_7_out);
  and and_6 (and_6_out, nand_1_out, nand_6_out, nand_7_out);
  and and_7 (and_7_out, nand_7_out, nand_8_out);
  and and_8 (and_8_out, nand_1_out, nand_6_out, nand_3_out);
  and and_9 (and_9_out, nand_5_out, nand_2_out, nand_3_out, not_1_out);
  and and_10 (and_10_out, nand_1_out, nand_2_out, nand_7_out);
  and and_11 (and_11_out, nand_5_out, nand_6_out, nand_7_out);
  buf buffer_3 (buffer_3_out, nand_5_out);
  and and_12 (and_12_out, nand_2_out, nand_7_out);
  and and_13 (and_13_out, nand_5_out, nand_6_out);
  and and_14 (and_14_out, nand_6_out, nand_3_out);
  and and_15 (and_15_out, nand_5_out, nand_3_out, not_1_out);
  and and_16 (and_16_out, nand_5_out, nand_6_out, nand_7_out);
  and and_17 (and_17_out, nand_2_out, nand_3_out, not_1_out, buffer_1_out);
  nor nor_1 (nor_1_out, and_1_out, and_2_out, and_3_out);
  nor nor_2 (nor_2_out, and_4_out, and_5_out, and_6_out);
  nor nor_3 (nor_3_out, and_7_out, and_8_out);
  nor nor_4 (nor_4_out, and_9_out, and_10_out, and_11_out);
  nor nor_5 (nor_5_out, buffer_3_out, and_12_out);
  nor nor_6 (nor_6_out, and_13_out, and_14_out, and_15_out);
  nor nor_7 (nor_7_out, and_16_out, and_17_out);
  not not_3 (Output_a, nor_1_out);
  not not_4 (Output_b, nor_2_out);
  not not_5 (Output_c, nor_3_out);
  not not_6 (Output_d, nor_4_out);
  not not_7 (Output_e, nor_5_out);
  not not_8 (Output_f, nor_6_out);
  not not_9 (Output_g, nor_7_out);
endmodule

module _74248 (
  input  Input_A,
  input  Input_B,
  input  Input_C,
  input  Input_D,
  input  BI___RBO,
  input  LT,
  input  RBI,
  output Output_a,
  output Output_b,
  output Output_c,
  output Output_d,
  output Output_e,
  output Output_f,
  output Output_g
);

  wire and_1_out, and_2_out, and_3_out, and_4_out, and_5_out, and_6_out, and_7_out, and_8_out, and_9_out,
       and_10_out, and_11_out, and_12_out, and_13_out, and_14_out, and_15_out, and_16_out, and_17_out,
       buffer_1_out, buffer_2_out, buffer_3_out, nand_1_out, nand_2_out, nand_3_out, nand_5_out, nand_6_out,
       nand_7_out, nand_8_out, not_1_out, not_2_out;

  nand nand_1 (nand_1_out, Input_A, buffer_1_out);
  nand nand_2 (nand_2_out, Input_B, buffer_1_out);
  nand nand_3 (nand_3_out, Input_C, buffer_1_out);
  not not_1 (not_1_out, Input_D);
  buf buffer_1 (buffer_1_out, LT);
  not not_2 (not_2_out, RBI);
  buf buffer_2 (buffer_2_out, BI___RBO);
  nand nand_4 (BI___RBO, buffer_1_out, not_2_out, not_1_out, nand_3_out, nand_2_out, nand_1_out);
  nand nand_5 (nand_5_out, nand_1_out, buffer_2_out);
  nand nand_6 (nand_6_out, nand_2_out, buffer_2_out);
  nand nand_7 (nand_7_out, nand_3_out, buffer_2_out);
  nand nand_8 (nand_8_out, not_1_out, buffer_2_out);
  and and_1 (and_1_out, nand_6_out, nand_8_out);
  and and_2 (and_2_out, nand_1_out, nand_2_out, nand_7_out);
  and and_3 (and_3_out, nand_5_out, nand_2_out, nand_3_out, not_1_out);
  and and_4 (and_4_out, nand_6_out, nand_8_out);
  and and_5 (and_5_out, nand_5_out, nand_2_out, nand_7_out);
  and and_6 (and_6_out, nand_1_out, nand_6_out, nand_7_out);
  and and_7 (and_7_out, nand_7_out, nand_8_out);
  and and_8 (and_8_out, nand_1_out, nand_6_out, nand_3_out);
  and and_9 (and_9_out, nand_5_out, nand_2_out, nand_3_out, not_1_out);
  and and_10 (and_10_out, nand_1_out, nand_2_out, nand_7_out);
  and and_11 (and_11_out, nand_5_out, nand_6_out, nand_7_out);
  buf buffer_3 (buffer_3_out, nand_5_out);
  and and_12 (and_12_out, nand_2_out, nand_7_out);
  and and_13 (and_13_out, nand_5_out, nand_6_out);
  and and_14 (and_14_out, nand_6_out, nand_3_out);
  and and_15 (and_15_out, nand_5_out, nand_3_out, not_1_out);
  and and_16 (and_16_out, nand_5_out, nand_6_out, nand_7_out);
  and and_17 (and_17_out, nand_2_out, nand_3_out, not_1_out, buffer_1_out);
  and and_18 (Output_a, ~and_1_out, ~and_2_out, ~and_3_out);  // AND_Gate
  and and_19 (Output_b, ~and_4_out, ~and_5_out, ~and_6_out);  // AND_Gate
  and and_20 (Output_c, ~and_7_out, ~and_8_out);  // AND_Gate
  and and_21 (Output_d, ~and_9_out, ~and_10_out, ~and_11_out);  // AND_Gate
  and and_22 (Output_e, ~buffer_3_out, ~and_12_out);  // AND_Gate
  and and_23 (Output_f, ~and_13_out, ~and_14_out, ~and_15_out);  // AND_Gate
  and and_24 (Output_g, ~and_16_out, ~and_17_out);  // AND_Gate
endmodule
